# Fritzing sketch MPU-6050 Board GY-521 Acelerometro Giroscopio (saved by Fritzing 0.9.2b)

parts:
  GY1 = MPU-6050 Board GY-521 [form="♀ (female)" package=THT]
  Composant1 = Arduino Uno (Rev3)

nets:
  N1: GY1.pin2, Composant1.GND
  N2: GY1.pin3, Composant1.A5/SCL
  N3: GY1.pin4, Composant1.A4/SDA
  N4: GY1.pin8, Composant1.D2

custom parts:
  MPU-6050 Board GY-521: Acelerometro y Giroscopio MPU-6050 Board GY-521
